# Fritzing sketch RiCino_TX-v2 (saved by Fritzing 0.8.3b)

parts:
  Parte1 = Arduino Pro Mini 3.3V
  S1 = Pushbutton [package="[THT]"]
  Q1 = NPN-Transistor [package="TO92 [THT]"]
  R1 = Resistor [tolerance=±5% resistance=10k package=THT]
  R2 = Resistor [tolerance=±5% resistance=10k package=THT]
  C1 = Electrolytic Capacitor [capacitance=1µF package="100 mil [THT, electrolytic]"]
  LED1 = LED - 5mm [color="Infrared (850nm)" package="5 mm [THT]"]
  R3 = Resistor [tolerance=±5% resistance=6.8 package=THT]
  J1 = female pin header, 2 pins [form="♀ (female)"]  # not connected

nets:
  N1: Parte1.VCC, S1.Pin_4, C1.+
  N2: Parte1.GND, Q1.E, R2.Pin_1, C1.-
  N3: Parte1.D10, S1.Pin_2, R2.Pin_0
  N4: Parte1.D3, R1.Pin_0
  N5: Q1.B, R1.Pin_1
  N6: Q1.C, LED1.cathode
  N7: LED1.anode, R3.Pin_0

notes:
  Led IR
  BC547
  e b c
  22uF/10V
  5V
  10k
  6,8ohm
