# Fritzing sketch RiCino_TX_simple (saved by Fritzing 0.8.3b)

parts:
  Parte1 = Arduino Pro Mini 3.3V
  Q1 = NPN-Transistor [package="TO92 [THT]"]
  R1 = Resistor [tolerance=±5% resistance=10k package=THT]
  LED1 = LED - 5mm [color="Infrared (850nm)" package="5 mm [THT]"]
  R3 = Resistor [tolerance=±5% resistance=6.8 package=THT]
  J1 = female pin header, 2 pins [form="♀ (female)"]

nets:
  N1: Parte1.VCC, J1.pin1
  N2: Parte1.GND, Q1.E, J1.pin2
  N3: Parte1.D3, R1.Pin_0
  N4: Q1.B, R1.Pin_1
  N5: Q1.C, LED1.cathode
  N6: LED1.anode, R3.Pin_0

notes:
  Led IR
  BC547
  e b c
  5V
  10k
  6,8ohm
