# Fritzing sketch RiCino_Zround (saved by Fritzing 0.8.3b)

parts:
  Parte1 = Arduino Uno (Rev3)
  R1 = Resistor [tolerance=±5% resistance=470 package=THT]
  R2 = Resistor [tolerance=±5% resistance=470 package=THT]
  LED1 = LED - 5mm [color="Red (633nm)" package="5 mm [THT]"]
  LED2 = LED - 5mm [color="Green (570nm)" package="5 mm [THT]"]
  IR1 = TSOP312.., 314.. [package=THT]  # not connected
  IR2 = TSOP312.., 314.. [package=THT]  # not connected
  IR3 = TSOP312.., 314.. [package=THT]  # not connected
  R3 = Resistor [tolerance=±5% resistance=100 package=THT]
  R4 = Resistor [tolerance=±5% resistance=100 package=THT]
  R5 = Resistor [tolerance=±5% resistance=100 package=THT]

nets:
  N1: Parte1.GND, LED1.cathode, LED2.cathode
  N2: Parte1.D8, R1.Pin_0
  N3: Parte1.D10_PWM/SS, R3.Pin_1, R4.Pin_1, R5.Pin_1
  N4: Parte1.D4, R2.Pin_0
  N5: R1.Pin_1, LED2.anode
  N6: R2.Pin_1, LED1.anode

notes:
  PUENTE
  TSOP 1730
  100 Ohm
  470 Ohm
  ROJO VERDE
  -----------------------------------------------------------------
  FLASH OFF - Sin conexión a Zround
  -----------------------------------------------------------------
  OFF ON - Carrera en marcha
